# Fritzing sketch Breadboard (saved by Fritzing 0.9.3b)

parts:
  RFM95W1 = RFM95W LoRa Module
  DS1 = DS18B20 1-Wire Temperature Sensor Probe
  Part1 = ADS1115
  BAT1 = Battery Holders [package=lipo-1100mAh]
  A1 = mini boost module
  ANT1 = Antenna
  M2 = DOIT Esp32 DevKit v1 (30 pins long, 11 pins width) [part_number=ESP32S-PIN30]
  HC-SR04_Sensor_1 = HC-SR04 Ultrasonic Distance Sensor
  R1 = Resistor [tolerance=±5% resistance=220 package="1206 [SMD]"]
  부품2 = FC-28 Soil Hygrometer Module - Probe  # not connected
  R2 = Resistor [tolerance=±5% resistance=220 package="0402 [SMD]"]

nets:
  N1: RFM95W1.2_MISO, M2.D19
  N2: RFM95W1.3_MOSI, M2.D23
  N3: RFM95W1.4_SCK, M2.D18
  N4: RFM95W1.5_NSS_(CS), M2.D13
  N5: RFM95W1.6_RESET, M2.D4
  N6: RFM95W1.9_ANT, ANT1.antenna_lead
  GND: RFM95W1.10_GND, Part1.GND, A1.Pin_3, M2.GND
  VDD: RFM95W1.13_3.3V, Part1.VDD, M2.3V3
  N7: RFM95W1.14_DIO0, M2.D27
  N8: RFM95W1.15_DIO1, M2.D26
  N9: DS1.DQ, M2.D25, R1.Pin_0
  N10: DS1.VDD, R1.Pin_1, R2.Pin_0
  N11: Part1.SCL, M2.D22
  N12: Part1.SDA, M2.D21
  N13: BAT1.+, A1.Pin_2
  N14: BAT1.-, A1.Pin_1
  N15: A1.Pin_4, M2.VIN
  N16: M2.D15, R2.Pin_1
  N17: M2.D32, HC-SR04_Sensor_1.ECHO
  N18: M2.D33, HC-SR04_Sensor_1.TRIG

notes:
  DIY TDS Sensor, using soil probe
  Dallas Temperature Sensor
  Ultrasonic sensor

custom parts:
  RFM95W LoRa Module: RF Transceiver by Hope RF. Well supported Arduino libraries are available. This Low Power Long Range Transceiver Module for the frequencies 868MHz and 915MHz and it is also available in other versions.
  ADS1115: ADC ADS1115
  mini boost module: mini boost module.
  DOIT Esp32 DevKit v1 (30 pins long, 11 pins width): The DOIT Esp32 DevKit v1 is one of the development board created by DOIT to evaluate the ESP-WROOM-32 module. It is based on the ESP32 microcontroller that boasts Wifi, Bluetooth, Ethernet and Low Power support all in a single chip. (vanepp) made breadboard work, adjusted pin numbering and labels and reduced size of schematic and cleaned up pcb. This chip is 30pins long (2 x15) and 11 pins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
  FC-28 Soil Hygrometer Module - Probe: The FC-28 is a soil hygrometer module that uses the Texas Instruments LM393 comparator chip to provide an analog measurement of soil humidity.
